# Fritzing sketch Untitled Sketch (saved by Fritzing 0.9.3b)
breadboards: 1

parts:
  Part1 = Arduino Mega 2560 (Rev3)
  J1 = Basic Servo
  J2 = Basic Servo
  J3 = Basic Servo
  Part2 = TFT 2.8 inch 320x240 Touch w microSD [part_number=1770]
  J4 = Basic Servo
  J5 = Piezo Speaker

nets:
  N1: Part1.D21/SCL, Part1.SCL, Part2.LCD_X-
  N2: Part1.D20/SDA, Part1.SDA, Part2.LCD_Y-
  N3: Part1.D13_PWM, J5.pin2
  N4: Part1.D12_PWM, J4.pulse
  N5: Part1.D11_PWM, J3.pulse
  N6: Part1.D10_PWM, J2.pulse
  N7: Part1.D9_PWM, J1.pulse
  VCC: Part1.5V, J1.vcc, J2.vcc, J3.vcc, Part2.+5V, J4.vcc
  GND: Part1.GND, J1.gnd, J2.gnd, J3.gnd, Part2.GND, J4.gnd, J5.pin1
  N8: Part1.D22, Part2.LCD_CS
  N9: Part1.D24, Part2.LCD_DC
  N10: Part1.D50, Part2.MISO
  N11: Part1.D51, Part2.MOSI
  N12: Part1.D52, Part2.SCLK

custom parts:
  TFT 2.8 inch 320x240 Touch w microSD: This TFT display is big (2.8" diagonal) bright (4 white-LED backlight) and colorful! 240x320 pixels with individual RGB pixel control. As a bonus, this display has a resistive touchscreen attached to it already, so you can detect finger presses anywhere on the screen.
